# Fritzing sketch proyecto (saved by Fritzing 0.9.0b)
breadboards: 1

parts:
  Raspberry_Pi_B_rev1 = Raspberry Pi B rev1
  S1 = Pushbutton [package="[THT]"]
  R1 = Resistor [tolerance=±5% resistance=10k package=THT]
  S2 = Pushbutton [package="[THT]"]
  R2 = Resistor [tolerance=±5% resistance=10k package=THT]
  S3 = Pushbutton [package="[THT]"]
  R3 = Resistor [tolerance=±5% resistance=10k package=THT]
  S4 = Pushbutton [package="[THT]"]
  R4 = Resistor [tolerance=±5% resistance=10k package=THT]
  S5 = Pushbutton [package="[THT]"]
  R5 = Resistor [tolerance=±5% resistance=10k package=THT]
  S6 = Pushbutton [package="[THT]"]
  R6 = Resistor [tolerance=±5% resistance=10k package=THT]
  J1 = Basic Servo
  LED1 = smd LED [color="Red (633nm)" package="0603 [SMD]"]
  R7 = Resistor [tolerance=±5% resistance=330 package=THT]
  LED2 = smd LED [color="Red (633nm)" package="0603 [SMD]"]
  R8 = Resistor [tolerance=±5% resistance=330 package=THT]

nets:
  5V: Raspberry_Pi_B_rev1.5V, S1.Pin_3, S1.Pin_4, S2.Pin_3, S2.Pin_4, S3.Pin_3, S3.Pin_4, S4.Pin_3, S4.Pin_4, S5.Pin_3, S5.Pin_4, S6.Pin_3, S6.Pin_4, J1.vcc
  GND: Raspberry_Pi_B_rev1.GND, R1.Pin_0, R2.Pin_0, R3.Pin_0, R4.Pin_0, R5.Pin_0, R6.Pin_0, J1.gnd, R7.Pin_0, R8.Pin_0
  N1: Raspberry_Pi_B_rev1.GPIO_23, S2.Pin_1, S2.Pin_2, R2.Pin_1
  N2: Raspberry_Pi_B_rev1.GPIO_18, S1.Pin_1, S1.Pin_2, R1.Pin_1
  N3: Raspberry_Pi_B_rev1.GPIO_24, S3.Pin_1, S3.Pin_2, R3.Pin_1
  N4: Raspberry_Pi_B_rev1.GPIO_10, LED2.anode
  N5: Raspberry_Pi_B_rev1.GPIO_9, LED1.anode
  N6: Raspberry_Pi_B_rev1.GPIO_25, S4.Pin_1, S4.Pin_2, R4.Pin_1
  N7: Raspberry_Pi_B_rev1.GPIO_11, J1.pulse
  N8: Raspberry_Pi_B_rev1.GPIO_8, S5.Pin_1, S5.Pin_2, R5.Pin_1
  N9: Raspberry_Pi_B_rev1.GPIO_7, S6.Pin_1, S6.Pin_2, R6.Pin_1
  N10: LED1.cathode, R7.Pin_1
  N11: LED2.cathode, R8.Pin_1
